# Fritzing sketch Snake Vision Robot (saved by Fritzing 0.9.3b)
breadboards: 1

parts:
  Part1 = Arduino Nano (Rev3.0)
  Part2 = Analog Digital MUX Breakout
  Part3 = Analog Digital MUX Breakout
  LED1 = LED - 5mm [color="Red (633nm)" package="5 mm [THT]"]
  VCC1 = 4 x AAA Battery Mount
  U1 = MLX90614 [package=to-39]
  U2 = MLX90614 [package=to-39]
  JP1 = Header 4 [package=jst-4-pth]  # not connected
  JP2 = Header 6 [package=molex-1x6_lock]

nets:
  GND: Part1.GND, LED1.anode, VCC1.-, U2.VSS, JP2.3
  N1: Part1.D3, JP2.1
  N2: Part1.D5, JP2.2
  N3: Part1.D6, JP2.5
  N4: Part1.D9, JP2.6
  N5: Part1.D12/MISO, LED1.cathode
  N6: Part1.VIN, VCC1.+, JP2.4
  5V: Part1.5V, U1.VDD
  N7: Part2.C0, U1.PWM_SDA
  N8: Part2.C1, U2.PWM_SDA
  N9: Part3.C0, U1.SCL_VZ
  N10: Part3.C1, U2.SCL_VZ

notes:
  To Motor A & B
  Left Motor is B side (2)
  Right Motor is A side (1)
  L9110 H Bridge
  6 Pin Connector
  Label From Top to Bottom
  Pin 1 B-IA
  Pin 2 B-IB
  Pin 3 GND
  Pin 4 VCC
  Pin 5 A-IA
  Pin 6 A-IB
  MUX 1 - SDA - A4
  MUX 2 - SCL - A5
  left sensor
  Right Sensor
